# Fritzing sketch ex02_LED_potentiometer_dimmer (saved by Fritzing 0.9.3b)
breadboards: 1

parts:
  Part1 = Arduino Uno (Rev3) - ICSP
  LED1 = LED - 5mm [color="Red (633nm)" package="5 mm [THT]"]  # not connected
  R2 = Resistor [tolerance=±5% resistance=330 package="2010 [SMD]"]
  R3 = TRIMPOT [package=3386u]

nets:
  N1: Part1.A0, R3.WIPER
  N2: Part1.5V, R3.CCW
  N3: Part1.GND, R2.Pin_0, R3.CW
