# Fritzing sketch ex03_pushbutton_LED (saved by Fritzing 0.9.3b)
breadboards: 1

parts:
  S1 = Momentary Switch [package=ksa_sealed_tac_switch]
  R1 = Resistor [tolerance=±5% resistance=10k package="2010 [SMD]"]
  Part1 = Arduino Uno (Rev3) - ICSP
  LED1 = LED - 5mm [color="Red (633nm)" package="5 mm [THT]"]
  R2 = Resistor [tolerance=±5% resistance=330 package="2010 [SMD]"]

nets:
  N1: S1.1, R1.Pin_1, Part1.D2
  N2: S1.3, Part1.GND, R2.Pin_0
  N3: R1.Pin_0, Part1.5V
  N4: Part1.D13/SCK, LED1.anode
  N5: LED1.cathode, R2.Pin_1
