# Fritzing sketch ex04_pushbuttons_LED (saved by Fritzing 0.9.3b)
breadboards: 1

parts:
  S1 = Momentary Switch [package=ksa_sealed_tac_switch]
  R1 = Resistor [tolerance=±5% resistance=10k package="2010 [SMD]"]
  Part1 = Arduino Uno (Rev3) - ICSP
  LED1 = LED - 5mm [color="Red (633nm)" package="5 mm [THT]"]
  R2 = Resistor [tolerance=±5% resistance=330 package="2010 [SMD]"]
  S2 = Momentary Switch [package=ksa_sealed_tac_switch]
  R3 = Resistor [tolerance=±5% resistance=10k package="2010 [SMD]"]

nets:
  N1: S1.1, R1.Pin_1, Part1.D2
  N2: S1.3, Part1.GND, R2.Pin_0, S2.3
  N3: R1.Pin_0, Part1.5V, R3.Pin_0
  N4: Part1.D13/SCK, LED1.anode
  N5: Part1.D3_PWM, S2.1, R3.Pin_1
  N6: LED1.cathode, R2.Pin_1
