# Fritzing sketch a00_pushbuttons_LEDs (saved by Fritzing 0.9.3b)
breadboards: 1

parts:
  S1 = Momentary Switch [package=ksa_sealed_tac_switch]
  R1 = Resistor [tolerance=±5% resistance=10k package="2010 [SMD]"]
  Part1 = Arduino Uno (Rev3) - ICSP
  S2 = Momentary Switch [package=ksa_sealed_tac_switch]
  R3 = Resistor [tolerance=±5% resistance=10k package="2010 [SMD]"]
  LED2 = LED - 5mm [color="Red (633nm)" package="5 mm [THT]"]
  LED3 = LED - 5mm [color="Red (633nm)" package="5 mm [THT]"]
  R4 = Resistor [tolerance=±5% resistance=330 package="2010 [SMD]"]
  R5 = Resistor [tolerance=±5% resistance=330 package="2010 [SMD]"]
  LED4 = LED - 5mm [color="Red (633nm)" package="5 mm [THT]"]
  S3 = Momentary Switch [package=ksa_sealed_tac_switch]
  R6 = Resistor [tolerance=±5% resistance=10k package="2010 [SMD]"]
  R7 = Resistor [tolerance=±5% resistance=330 package="2010 [SMD]"]
  S4 = Momentary Switch [package=ksa_sealed_tac_switch]
  LED5 = LED - 5mm [color="Red (633nm)" package="5 mm [THT]"]
  R8 = Resistor [tolerance=±5% resistance=330 package="2010 [SMD]"]

nets:
  N1: S1.1, R1.Pin_1, Part1.D2
  N2: S1.3, Part1.GND, S2.3, R4.Pin_0, R5.Pin_0, S3.3, R7.Pin_0, S4.3
  N3: R1.Pin_0, Part1.5V, R3.Pin_0, R6.Pin_0
  N4: Part1.D9_PWM, LED2.anode
  N5: Part1.D10_PWM/SS, LED3.anode
  N6: Part1.D11_PWM/MOSI, LED4.anode
  N7: Part1.D12/MISO, LED5.anode
  N8: Part1.D3_PWM, S2.1, R3.Pin_1
  N9: Part1.D4, S3.1, R6.Pin_1
  N10: Part1.D5_PWM, S4.1
  N11: LED2.cathode, R4.Pin_1
  N12: LED3.cathode, R5.Pin_1
  N13: LED4.cathode, R7.Pin_1
  N14: LED5.cathode, R8.Pin_1
